# Fritzing sketch pir_sensor (saved by Fritzing 0.9.3b)

parts:
  Raspberry_Pi1 = Raspberry Pi B+
  PIR1 = PIR sensor

nets:
  N1: Raspberry_Pi1.GPIO17, PIR1.SIG
  GND: Raspberry_Pi1.GND, PIR1.GND
  5V: Raspberry_Pi1.5V, PIR1.VDD
